# Fritzing sketch 2wd_robocar (saved by Fritzing 1.0.7)

parts:
  Bauteil1 = Arduino Uno (Rev3) - ICSP  # not connected
  M1 = DC Motor [voltage_(max)=6V voltage_(min)=3V]
  S1 = H-Bridge with L298N
  M2 = DC Motor [voltage_(max)=6V voltage_(min)=3V]
  HC-SR04_Sensor_1 = HC-SR04 Ultrasonic Distance Sensor
  S3 = Toggle Switch [package=THT]  # not connected
  Bauteil2 = Arduino Sensor Shield v5.0
  VCC2 = Battery
  J1 = Basic Servo  # not connected

nets:
  N1: M1.pin_1, S1.M1-01
  N2: M1.pin_2, S1.M1-02
  N3: S1.GND, VCC2.-
  N4: S1.ENA, S1.ENA-5V
  N5: S1.IN1, Bauteil2.D5
  N6: S1.IN2, Bauteil2.D6
  N7: S1.IN3, Bauteil2.D9
  N8: S1.IN4, Bauteil2.D10
  N9: S1.ENB, S1.ENB-5V
  N10: S1.M2-01, M2.pin_2
  N11: S1.M2-02, M2.pin_1
  VCC: HC-SR04_Sensor_1.VCC, Bauteil2.+5V
  N12: HC-SR04_Sensor_1.TRIG, Bauteil2.D11
  N13: HC-SR04_Sensor_1.ECHO, Bauteil2.D12
  GND: HC-SR04_Sensor_1.GND, Bauteil2.GND

notes:
  2 wheels drive robo car

custom parts:
  H-Bridge with L298N: h-bridge
  Battery: Your standard 2x 18650 battery pack (7.4 Volts)
